// Logisim project wikiarduino.circ as structural Verilog: 3 circuits, main circuit main
// Reset button
module main (
  input  _9,
  input  _8,
  input  _7,
  input  _6,
  input  _5,
  input  _4,
  input  _3,
  input  in_8,
  input  in_9,
  input  in_10,
  input  in_11,
  input  in_12,
  input  in_13,
  output _2,
  output a0,
  output a1,
  output a2,
  output a3,
  output a4,
  output a5
);

  wire Reset_Button_out;
  wire [7:0] decoder_1_out0, n8_bit_register_1_output;

  Button Reset_Button (.out(Reset_Button_out));
  Decoder #(.select(3), .enable("false")) decoder_1 (
    .out0(decoder_1_out0[0]), .out1(decoder_1_out0[1]), .out2(decoder_1_out0[2]), .out3(decoder_1_out0[3]),
    .out4(decoder_1_out0[4]), .out5(decoder_1_out0[5]), .out6(decoder_1_out0[6]), .out7(decoder_1_out0[7]),
    .sel({_7, _6, _5}));
  LED led_1 (.in(n8_bit_register_1_output[7]));
  _8_bit_register u_8_bit_register_1 (
    .Clock(_3), .address(decoder_1_out0), .Data(_4), .Reset(Reset_Button_out),
    .Output(n8_bit_register_1_output));
  LED led_2 (.in(n8_bit_register_1_output[3]));
  LED led_3 (.in(n8_bit_register_1_output[4]));
  LED led_4 (.in(n8_bit_register_1_output[6]));
  LED led_5 (.in(n8_bit_register_1_output[5]));
  LED led_6 (.in(n8_bit_register_1_output[0]));
  LED led_7 (.in(n8_bit_register_1_output[1]));
  LED led_8 (.in(n8_bit_register_1_output[2]));
  Multiplexer #(.select(3), .enable("false")) multiplexer_1 (
    .in0(n8_bit_register_1_output[0]), .in1(n8_bit_register_1_output[1]), .in2(n8_bit_register_1_output[2]),
    .in3(n8_bit_register_1_output[3]), .in4(n8_bit_register_1_output[4]), .in5(n8_bit_register_1_output[5]),
    .in6(n8_bit_register_1_output[6]), .in7(n8_bit_register_1_output[7]), .out(_2), .sel({_7, _6, _5}));

  assign a0 = in_8;
  assign a1 = in_9;
  assign a2 = in_10;
  assign a3 = in_11;
  assign a4 = in_12;
  assign a5 = in_13;

  // Notes on the sheet:
  //   il numero sotto il pin è il numero del pin sulla board di arduino
  //   pin 3 rappresenta il clock
  //   pin 4 rappresenta il nuovo dato
  //   pin 2 rappresenta il valore salvato
  //   pin 5-6-7 rappresentano l'indirizzo
  //   collegamento con i sensori ... il pin a0 gestisce unicamente il sensore di temperatura
  //   quindi contiene al suo interno già la conversione in temperatura
  //   gli altri pin invece restituiscono semplicemente il valore grezzo
endmodule

module register (
  input  Data,
  input  Clock,
  input  Reset,
  output Output,
  output out_5
);

  wire and_1_out, and_2_out, not_1_out, or_1_out;

  not not_1 (not_1_out, Data);
  and and_1 (and_1_out, not_1_out, Clock);
  and and_2 (and_2_out, Clock, Data);
  or or_1 (or_1_out, Reset, and_1_out);
  nor nor_1 (Output, or_1_out, out_5);
  nor nor_2 (out_5, Output, and_2_out);
endmodule

module _8_bit_register (
  input  Clock,
  input  [7:0] address,
  input  Data,
  input  Reset,
  output [7:0] Output
);

  wire and_1_out, and_2_out, and_3_out, and_4_out, and_5_out, and_6_out, and_7_out, and_8_out;

  and and_1 (and_1_out, address[0], Clock);
  and and_2 (and_2_out, address[1], Clock);
  and and_3 (and_3_out, address[2], Clock);
  and and_4 (and_4_out, address[3], Clock);
  and and_5 (and_5_out, address[4], Clock);
  and and_6 (and_6_out, address[5], Clock);
  and and_7 (and_7_out, address[6], Clock);
  and and_8 (and_8_out, address[7], Clock);
  register register_1 (.Data(Data), .Clock(and_1_out), .Reset(Reset), .Output(Output[0]));  // open: out_5
  register register_2 (.Data(Data), .Clock(and_2_out), .Reset(Reset), .Output(Output[1]));  // open: out_5
  register register_3 (.Data(Data), .Clock(and_3_out), .Reset(Reset), .Output(Output[2]));  // open: out_5
  register register_4 (.Data(Data), .Clock(and_4_out), .Reset(Reset), .Output(Output[3]));  // open: out_5
  register register_5 (.Data(Data), .Clock(and_5_out), .Reset(Reset), .Output(Output[4]));  // open: out_5
  register register_6 (.Data(Data), .Clock(and_6_out), .Reset(Reset), .Output(Output[5]));  // open: out_5
  register register_7 (.Data(Data), .Clock(and_7_out), .Reset(Reset), .Output(Output[6]));  // open: out_5
  register register_8 (.Data(Data), .Clock(and_8_out), .Reset(Reset), .Output(Output[7]));  // open: out_5
endmodule
